# Fritzing sketch lamp (saved by Fritzing 0.9.10b)
breadboards: 1

parts:
  Mod1 = Amica NodeMCU DEVKIT 1.0
  U1 = POT [knob_status=50% power=0.5W package=pot_mammoth]
  S1 = Pushbutton [package="[THT]"]
  R1 = Resistor [tolerance=±5% resistance=220 package="2512 [SMD]"]
  R2 = Resistor [tolerance=±5% resistance=10000 package="0402 [SMD]"]
  Part1 = ws2812b [package="smd 2812b"]

nets:
  N1: Mod1.pin1, Mod1.pin_10, Mod1.pin_26, U1.S, R2.Pin_1
  N2: Mod1.pin2, Mod1.pin_9, Mod1.pin_25, Mod1.pin_29, U1.E, R1.Pin_0
  N3: Mod1.pin7, Part1.DIN
  N4: Mod1.pin8, S1.Pin_3, S1.Pin_4, R2.Pin_0
  N5: Mod1.pin_16, U1.A
  N6: S1.Pin_1, S1.Pin_2, R1.Pin_1
